// Logisim project SUBLEQ_computer.circ as structural Verilog: 1 circuit, main circuit main
module main (
  input  in_1
);

  wire and_1_out, and_2_out, and_3_out, and_4_out, clock_1_out, decoder_1_out0, decoder_1_out1,
       decoder_1_out2, decoder_1_out3, decoder_1_out4, decoder_1_out5, decoder_1_out6, decoder_1_out7,
       nor_1_out, not_2_out, or_1_out, or_2_out, or_3_out, or_4_out, or_5_out, or_6_out;
  wire [2:0] counter_2_q;
  wire [15:0] adder_1_out, controlled_buffer_1_out, controlled_buffer_2_out, counter_1_q, not_1_out,
       register_1_q, register_2_q, register_3_q;

  Clock clock_1 (.out(clock_1_out));
  Register #(.width(16)) register_1 (
    .D(controlled_buffer_1_out), .en(or_2_out), .Q(register_1_q), .clk(clock_1_out), .clr(in_1));
  Counter #(.width(16), .max('hffff)) counter_1 (
    .load(and_3_out), .D(controlled_buffer_2_out), .count(or_3_out), .Q(counter_1_q), .clk(clock_1_out),
    .clr(in_1));  // open: carry
  Register #(.width(16)) register_2 (
    .D(controlled_buffer_1_out), .en(decoder_1_out1), .Q(register_2_q), .clk(clock_1_out), .clr(in_1));
  assign not_1_out = ~register_3_q;  // NOT_Gate not_1, 16 bits wide
  Register #(.width(16)) register_3 (
    .D(controlled_buffer_1_out), .en(decoder_1_out3), .Q(register_3_q), .clk(clock_1_out), .clr(in_1));
  assign controlled_buffer_1_out = decoder_1_out4 ? adder_1_out : 16'bz;  // Controlled_Buffer controlled_buffer_1
  assign controlled_buffer_2_out = or_1_out ? register_1_q : 16'bz;  // Controlled_Buffer controlled_buffer_2
  assign controlled_buffer_2_out = or_2_out ? counter_1_q : 16'bz;  // Controlled_Buffer controlled_buffer_3
  and and_1 (and_1_out, not_2_out, or_4_out);
  not not_2 (not_2_out, controlled_buffer_2_out[15]);
  Adder #(.width(16)) adder_1 (.a(register_2_q), .b(not_1_out), .out(adder_1_out), .cin(1'b1));  // open: cout
  or or_1 (or_1_out, decoder_1_out1, decoder_1_out3, decoder_1_out4, and_3_out);
  or or_2 (or_2_out, decoder_1_out0, decoder_1_out2, decoder_1_out5);
  and and_2 (and_2_out, clock_1_out, decoder_1_out4);
  nor nor_1 (nor_1_out, adder_1_out[0], adder_1_out[1], adder_1_out[2], adder_1_out[3], adder_1_out[4], adder_1_out[5], adder_1_out[6], adder_1_out[7], adder_1_out[9], adder_1_out[10], adder_1_out[11], adder_1_out[12], adder_1_out[13], adder_1_out[14], adder_1_out[15], adder_1_out[8]);
  ROM #(.addrWidth(16), .dataWidth(16)) rom_1 (
    .addr(controlled_buffer_2_out), .data(controlled_buffer_1_out), .sel(and_1_out));
  RAM #(.addrWidth(16), .dataWidth(16)) ram_1 (
    .addr(controlled_buffer_2_out), .data(controlled_buffer_1_out), .sel(controlled_buffer_2_out[15]),
    .clk(and_2_out), .ld(or_4_out), .clr(in_1));
  or or_3 (or_3_out, decoder_1_out1, decoder_1_out3, and_4_out);
  or or_4 (or_4_out, decoder_1_out0, decoder_1_out1, decoder_1_out2, decoder_1_out3, decoder_1_out5);
  and and_3 (and_3_out, or_6_out, decoder_1_out6);
  Counter #(.width(3), .max('h7)) counter_2 (
    .load(1'b0), .count(1'b1), .Q(counter_2_q), .clk(clock_1_out), .clr(or_5_out));  // open: D, carry
  or or_5 (or_5_out, in_1, decoder_1_out7);
  or or_6 (or_6_out, nor_1_out, adder_1_out[15]);
  and and_4 (and_4_out, ~or_6_out, decoder_1_out6);  // AND_Gate
  Decoder #(.select(3)) decoder_1 (
    .out0(decoder_1_out0), .out1(decoder_1_out1), .out2(decoder_1_out2), .out3(decoder_1_out3),
    .out4(decoder_1_out4), .out5(decoder_1_out5), .out6(decoder_1_out6), .out7(decoder_1_out7),
    .sel(counter_2_q), .en(1'b1));
endmodule
