// Logisim project Transport Triggered.circ as structural Verilog: 2 circuits, main circuit main
module main (
  input  in_1
);

  wire clock_1_out, exicution_unit_1_romselect;
  wire [15:0] exicution_unit_1_adress, exicution_unit_1_generaloutput1, rom_1_data;

  Clock clock_1 (.out(clock_1_out));
  Exicution_Unit exicution_unit_1 (
    .Reset(in_1), .Clock(clock_1_out), .GeneralOutput1(exicution_unit_1_generaloutput1), .Data(rom_1_data),
    .Adress(exicution_unit_1_adress), .RomSelect(exicution_unit_1_romselect));  // open: WriteTo, ReadFrom, GeneralInput1, GeneralOutput2, GeneralInput2
  // Probe on exicution_unit_1_generaloutput1
  ROM #(.addrWidth(16), .dataWidth(16)) rom_1 (
    .addr(exicution_unit_1_adress), .data(rom_1_data), .sel(exicution_unit_1_romselect));

  // Notes on the sheet:
  //   contents of rom_1 (hex, n*v repeats v):
  //   0 0 fe fff8 ff fff9 fffb 100 100 fff7 fd ffff 241*0 a 2 3
endmodule

module Exicution_Unit (
  input  Reset,
  input  Clock,
  input  [15:0] Data,
  output WriteTo,
  output ReadFrom,
  output [15:0] GeneralOutput1,
  output [15:0] GeneralInput1,
  output [15:0] GeneralOutput2,
  output [15:0] GeneralInput2,
  output [15:0] Adress,
  output RomSelect
);

  wire adder_1_cout, and_1_out, and_2_out, and_3_out, and_4_out, and_5_out, and_6_out, and_8_out, and_9_out,
       and_10_out, and_11_out, and_12_out, and_14_out, and_15_out, and_16_out, decoder_1_out0,
       decoder_1_out1, decoder_1_out2, decoder_2_out4, decoder_2_out5, decoder_2_out6, decoder_2_out7,
       decoder_3_out4, decoder_3_out5, decoder_3_out6, decoder_3_out7, decoder_4_out0, decoder_4_out1,
       decoder_4_out2, decoder_4_out3, decoder_4_out4, decoder_4_out5, decoder_4_out6, decoder_4_out7,
       nand_1_out, nand_2_out, not_1_out, not_2_out, not_4_out, or_1_out, or_2_out, or_3_out, or_4_out,
       or_5_out, or_6_out, or_9_out, or_10_out, or_11_out;
  wire [1:0] counter_2_q;
  wire [15:0] adder_1_out, and_7_out, counter_1_q, not_3_out, or_7_out, register_1_q, register_2_q,
       register_3_q, register_4_q, xor_1_out;

  not not_1 (not_1_out, Clock);
  not not_2 (not_2_out, or_2_out);
  or or_1 (or_1_out, and_1_out, and_2_out);
  and and_1 (and_1_out, or_2_out, Clock);
  or or_2 (or_2_out, decoder_4_out7, and_8_out, and_6_out, and_3_out);
  assign Data = WriteTo ? register_1_q : 16'bz;  // Controlled_Buffer controlled_buffer_1
  Register #(.width(16)) register_1 (.D(Data), .en(decoder_1_out1), .Q(register_1_q), .clk(Clock), .clr(Reset));
  assign Adress = or_3_out ? register_2_q : 16'bz;  // Controlled_Buffer controlled_buffer_2
  Register #(.width(16)) register_2 (.D(Data), .en(or_4_out), .Q(register_2_q), .clk(Clock), .clr(Reset));
  assign Adress = or_5_out ? counter_1_q : 16'bz;  // Controlled_Buffer controlled_buffer_3
  Counter #(.width(16), .max('hffff)) counter_1 (
    .load(or_2_out), .D(Data), .count(not_2_out), .Q(counter_1_q), .clk(or_1_out), .clr(Reset));  // open: carry
  and and_2 (and_2_out, or_6_out, ~or_2_out);  // AND_Gate
  Counter #(.width(2), .max('h3)) counter_2 (
    .load(1'b0), .count(1'b1), .Q(counter_2_q), .clk(not_1_out), .clr(Reset));  // open: D, carry
  or or_3 (or_3_out, decoder_1_out1, WriteTo);
  or or_4 (or_4_out, decoder_1_out0, decoder_1_out2);
  or or_5 (or_5_out, decoder_1_out0, decoder_1_out2);
  or or_6 (or_6_out, decoder_1_out1, WriteTo);
  and and_3 (and_3_out, nand_1_out, decoder_4_out4);
  Decoder #(.select(2)) decoder_1 (
    .out0(decoder_1_out0), .out1(decoder_1_out1), .out2(decoder_1_out2), .out3(WriteTo), .sel(counter_2_q),
    .en(1'b1));
  and and_4 (and_4_out, Adress[3], Adress[4], Adress[5], Adress[6], Adress[7], Adress[8], Adress[9], Adress[10], Adress[11], Adress[12], Adress[13], Adress[14], Adress[15]);
  and and_5 (and_5_out, Adress[3], ~Adress[4], Adress[5], Adress[6], Adress[7], Adress[8], Adress[9], Adress[10], Adress[11], Adress[12], Adress[13], Adress[14], Adress[15]);  // AND_Gate
  Register #(.width(16)) register_3 (.D(Data), .en(decoder_4_out1), .Q(register_3_q), .clk(Clock), .clr(Reset));
  Register #(.width(16)) register_4 (.D(Data), .en(decoder_4_out0), .Q(register_4_q), .clk(Clock), .clr(Reset));
  nand nand_1 (nand_1_out, adder_1_out[0], adder_1_out[1], adder_1_out[2], adder_1_out[3], adder_1_out[4], adder_1_out[5], adder_1_out[6], adder_1_out[7], adder_1_out[9], adder_1_out[10], adder_1_out[11], adder_1_out[12], adder_1_out[13], adder_1_out[14], adder_1_out[15], adder_1_out[8]);
  and and_6 (and_6_out, adder_1_out[15], decoder_4_out5);
  // Probe on Data
  // Probe on Adress
  Decoder #(.select(3), .disabled(0)) decoder_2 (
    .out4(decoder_2_out4), .out5(decoder_2_out5), .out6(decoder_2_out6), .out7(decoder_2_out7),
    .sel(Adress[2:0]), .en(and_5_out));  // open: out0, out1, out2, out3
  assign Data = decoder_2_out4 ? not_3_out : 16'bz;  // Controlled_Buffer controlled_buffer_4
  assign not_3_out = ~register_3_q;  // NOT_Gate not_3, 16 bits wide
  assign and_7_out = register_3_q & register_4_q;  // AND_Gate and_7, 16 bits wide
  assign Data = decoder_2_out5 ? and_7_out : 16'bz;  // Controlled_Buffer controlled_buffer_5
  assign or_7_out = register_3_q | register_4_q;  // OR_Gate or_7, 16 bits wide
  assign Data = decoder_2_out6 ? or_7_out : 16'bz;  // Controlled_Buffer controlled_buffer_6
  assign Data = decoder_2_out7 ? xor_1_out : 16'bz;  // Controlled_Buffer controlled_buffer_7
  assign xor_1_out = register_3_q ^ register_4_q;  // XOR_Gate xor_1, 16 bits wide
  Adder #(.width(16)) adder_1 (
    .a(register_3_q), .b(register_4_q), .out(adder_1_out), .cin(decoder_4_out2), .cout(adder_1_cout));
  and and_8 (and_8_out, adder_1_cout, decoder_4_out6);
  or or_8 (ReadFrom, decoder_1_out0, decoder_1_out1, decoder_1_out2);
  Decoder #(.select(3), .disabled(0)) decoder_3 (
    .out4(decoder_3_out4), .out5(decoder_3_out5), .out6(decoder_3_out6), .out7(decoder_3_out7),
    .sel(Adress[2:0]), .en(and_9_out));  // open: out0, out1, out2, out3
  and and_9 (and_9_out, ~Adress[3], Adress[4], Adress[5], Adress[6], Adress[7], Adress[8], Adress[9], Adress[10], Adress[11], Adress[12], Adress[13], Adress[14], Adress[15]);  // AND_Gate
  Decoder #(.select(3), .disabled(0)) decoder_4 (
    .out0(decoder_4_out0), .out1(decoder_4_out1), .out2(decoder_4_out2), .out3(decoder_4_out3),
    .out4(decoder_4_out4), .out5(decoder_4_out5), .out6(decoder_4_out6), .out7(decoder_4_out7),
    .sel(Adress[2:0]), .en(and_4_out));
  or or_9 (or_9_out, decoder_4_out2, decoder_4_out3);
  assign Data = or_9_out ? adder_1_out : 16'bz;  // Controlled_Buffer controlled_buffer_8
  nand nand_2 (nand_2_out, Adress[15], Adress[14], Adress[13], Adress[12], Adress[10], Adress[9], Adress[8], Adress[11]);
  and and_10 (and_10_out, nand_2_out, or_10_out);
  Register #(.width(16)) register_5 (.D(Data), .en(decoder_3_out5), .Q(GeneralOutput2), .clk(Clock), .clr(Reset));
  Register #(.width(16)) register_6 (.D(Data), .en(decoder_3_out7), .Q(GeneralOutput1), .clk(Clock), .clr(Reset));
  or or_10 (or_10_out, Adress[15], Adress[14], Adress[13], Adress[12], Adress[10], Adress[9], Adress[8], Adress[11]);
  not not_4 (not_4_out, or_10_out);
  and and_11 (and_11_out, ReadFrom, decoder_3_out6);
  and and_12 (and_12_out, ReadFrom, decoder_3_out4);
  assign Data = and_11_out ? GeneralInput1 : 16'bz;  // Controlled_Buffer controlled_buffer_9
  and and_13 (RomSelect, not_4_out, ReadFrom);
  and and_14 (and_14_out, WriteTo, Clock);
  or or_11 (or_11_out, ReadFrom, WriteTo);
  assign Data = and_12_out ? GeneralInput2 : 16'bz;  // Controlled_Buffer controlled_buffer_10
  and and_15 (and_15_out, or_11_out, and_10_out);
  and and_16 (and_16_out, ReadFrom, and_10_out);
  RAM #(.addrWidth(16), .dataWidth(16)) ram_1 (
    .addr(Adress), .data(Data), .sel(and_15_out), .clk(and_14_out), .ld(and_16_out), .clr(Reset));
endmodule
